# Fritzing sketch RFLink Gatway (saved by Fritzing 0.9.3b)
breadboards: 1

parts:
  NodeMCU1 = NodeMCU V1.0 [part_number=A]
  Part1 = Logic Level Converter
  R1 = Resistor [tolerance=±5% resistance=471 package="0603 [SMD]"]
  R2 = Resistor [tolerance=±5% resistance=471 package="0603 [SMD]"]
  R3 = Resistor [tolerance=±5% resistance=471 package="0603 [SMD]"]
  R4 = Resistor [tolerance=±5% resistance=471 package="0603 [SMD]"]
  U3 = V_REG_MIC2920 [package=sot223]
  Part2 = Arduino Mega 2560 (Rev3)
  SRX882 = female pin header, 4 pins [form="♀ (female)"]
  STX882 = female pin header, 3 pins [form="♀ (female)"]
  CC2500 = female pin header, 8 pins [form="♀ (female)"]

nets:
  GND: NodeMCU1.GND, NodeMCU1.Vin, Part1.GND, U3.GND, Part2.GND, Part2.D6_PWM, Part2.D7_PWM, SRX882.pin1, STX882.pin1, CC2500.pin7
  N1: NodeMCU1.RX, Part1.TX2_LV
  N2: NodeMCU1.TX, Part1.RX2_LV
  N3: Part1.LV, U3.OUT, CC2500.pin8
  N4: Part1.HV, U3.IN, Part2.5V, SRX882.pin4, STX882.pin2
  N5: Part1.RX2_HV, Part2.D0_RX0
  N6: Part1.TX2_HV, Part2.D1_TX0
  N7: R1.Pin_0, CC2500.pin6
  N8: R1.Pin_1, Part2.D51
  N9: R2.Pin_0, CC2500.pin5
  N10: R2.Pin_1, Part2.D52
  N11: R3.Pin_0, CC2500.pin4
  N12: R3.Pin_1, Part2.D50
  N13: R4.Pin_0, CC2500.pin1
  N14: R4.Pin_1, Part2.D47
  N15: Part2.D19/RX1, SRX882.pin2
  N16: Part2.D15/RX3, STX882.pin3

custom parts:
  NodeMCU V1.0: ESP8266 based NodeMCU
